# Fritzing sketch client_design (saved by Fritzing 0.9.3b)
perfboards: 1

parts:
  X1 = USB Connectors [package=usb-microb]  # not connected
  Raspberry_Pi_1 = Raspberry Pi 3 [part_number=RPI-3-V1.2]
  Part3 = RFID-RC522-v2
  LED1 = RGB LED (com. cathode, rgb) [package="5 mm [THT]"]  # not connected
  LED2 = RGB LED (com. cathode, rgb) [package="5 mm [THT]"]  # not connected
  LED3 = RGB LED (com. cathode, rgb) [package="5 mm [THT]"]  # not connected

nets:
  3V3: Raspberry_Pi_1.3v3, Raspberry_Pi_1.3V3, Part3.3_3V
  N1: Raspberry_Pi_1.GPIO10, Part3.MOSI
  N2: Raspberry_Pi_1.GPIO9, Part3.MISO
  N3: Raspberry_Pi_1.GPIO11, Part3.SCK
  N4: Raspberry_Pi_1.GND, Part3.SDA
  N5: Raspberry_Pi_1.GPIO8, Part3.GND
  N6: Raspberry_Pi_1.GPIO25, Part3.RST

custom parts:
  RFID-RC522-v2: A simple China made RFID-RC522 Reader; do check the pin labels, as this is a MFRC522 based clone.
